# Fritzing sketch water_level_sch (saved by Fritzing 0.9.10b)
breadboards: 1

parts:
  Q1 = NPN-Transistor [package="TO92 [THT]"]
  D1 = Diode [package=diode-1n4001]
  R1 = Resistor [tolerance=±5% power=0.25 resistance=10 package=THT]
  R2 = Resistor [tolerance=±5% power=0.25 resistance=2200 package=THT]
  R3 = Resistor [tolerance=±5% power=0.25 resistance=2200 package=THT]
  R4 = Resistor [tolerance=±5% power=0.25 resistance=1000 package=THT]
  U2 = 4001 4 x 2 Input NOR Gate, single part [part_number=4001 package="DIP (Dual Inline) [THT]"]
  R5 = Resistor [tolerance=±5% power=0.25 resistance=2200 package=THT]
  R6 = Resistor [tolerance=±5% power=0.25 resistance=2200 package=THT]
  U4 = SWITCH-SPST-2 [package=r_sw_th]
  U3 = SWITCH-SPST-2 [package=r_sw_th]
  U1 = RELAY [package=relay-t9a]
  U1_2 = RELAY [package=relay-g5q]
  BULB2 = Incandescent light bulb small [package="bulb sm"]  # not connected

nets:
  N1: Q1.E, R1.Pin_0
  N2: Q1.B, R3.Pin_1
  N3: Q1.C, D1.A, U1.COIL2, U1_2.COIL2
  5V: D1.C, U2.VDD, U4.P, U3.P, U1.COIL1, U1_2.COIL1
  GND: R1.Pin_1, R2.Pin_1, R4.Pin_1, U2.A1, U1.NO, U1_2.NO
  N4: R3.Pin_0, U2.B3, U2.Q4
  N5: R4.Pin_0, U2.Q3, U2.A4
  N6: U2.A3, R5.Pin_0
  N7: U2.B4, R6.Pin_1
  N8: R5.Pin_1, U4.O
  N9: R6.Pin_0, U3.O
  N10: U1.MAIN, U1_2.MAIN

notes:
  115Vac Main
  Mains Neutral
  115Vac 60 Watt
  5VDC
  SR NOR Latch
  5VDC relay
  2n3904
  1n4001
  Circuit ground
